# Fritzing sketch wiring-sketch (saved by Fritzing 0.9.3b)
breadboards: 1

parts:
  S1 = Pushbutton [package="[THT]"]
  Part1 = Arduino Uno (Rev3)
  J1 = Piezo Speaker  # not connected
  LED1 = RGB LED (com. cathode, rgb) [package="5 mm [THT]"]
  R1 = Resistor [tolerance=±5% resistance=330 package=THT]
  hc-sr1 = hc-sr04
  R2 = Resistor [tolerance=±5% resistance=330 package=THT]
  R3 = Resistor [tolerance=±5% resistance=330 package=THT]

nets:
  N1: S1.Pin_1, S1.Pin_2
  N2: S1.Pin_3, S1.Pin_4
  5V: Part1.5V, hc-sr1.VCC
  GND: Part1.GND, LED1.common_cathode, hc-sr1.GND
  N3: LED1.red_anode, R1.Pin_0
  N4: LED1.green_anode, R2.Pin_0
  N5: LED1.blue_anode, R3.Pin_0
